# Fritzing sketch connections (saved by Fritzing 0.9.1b)

parts:
  Part1 = Arduino Uno (Rev3)
  MOTOR1 = 28BYJ-48 Stepper Motor  # not connected
  X1 = X113647 Stepper Driver Board [package=board]
  Power_plug1 = Power plug

nets:
  N1: Part1.D8, X1.IN1
  N2: Part1.D9_PWM, X1.IN2
  N3: Part1.D10_PWM/SS, X1.IN3
  N4: Part1.D11_PWM/MOSI, X1.IN4
  GND: X1.GND, Power_plug1.GND
  N5: X1.+V, Power_plug1.VCC

notes:
  to DC 5v 100mA+
  Arduino to USB or DC power
  28BYJ-48 Stepper Motor

custom parts:
  28BYJ-48 Stepper Motor: 28BYJ-48 gear-reduction stepper motor (small)
  X113647 Stepper Driver Board: A common stepper motor driver board based on ULN2003APG darlington array
